# Fritzing sketch Carro (saved by Fritzing 0.9.10b)
breadboards: 1

parts:
  Componente1 = NRF24L01+ Breakout Board
  S6 = SPST Switch [package=r_sw_th]
  Componente2 = Arduino Pro Mini v13
  U1 = V_REG_LD1117VXX [package=78xxl]
  C1 = Electrolytic Capacitor [capacitance=1µF package="100 mil [THT, electrolytic]"]
  M1 = DC Motor [voltage_(max)=6V voltage_(min)=3V]
  L298N1 = L298N DC motor driver
  M2 = DC Motor [voltage_(max)=6V voltage_(min)=3V]
  BAT1 = 18650 battery holder [package=battery-18650-kit]
  BAT2 = 18650 battery holder [package=battery-18650-kit]

nets:
  GND: Componente1.GND, Componente2.GND, U1.GND, C1.-, L298N1.GND, BAT2.-
  N1: Componente1.VCC, U1.OUT
  N2: Componente1.CE, Componente2.D9_PWM
  N3: Componente1.CS, Componente2.D10_PWM/SS
  N4: Componente1.SCK, Componente2.D13/SCK
  N5: Componente1.MOSI, Componente2.D11_PWM/MOSI
  N6: Componente1.MISO, Componente2.D12/MISO
  N7: S6.P, Componente2.RAW, U1.IN, C1.+
  N8: S6.S, L298N1.5V
  N9: Componente2.D6_PWM, L298N1.IN4
  N10: Componente2.D5_PWM, L298N1.IN3
  N11: Componente2.D4, L298N1.IN2
  N12: Componente2.D3_PWM, L298N1.IN1
  N13: M1.pin_1, L298N1.OUT2
  N14: M1.pin_2, L298N1.OUT1
  N15: L298N1.OUT3, M2.pin_2
  N16: L298N1.OUT4, M2.pin_1
  N17: L298N1.12V, BAT1.+
  N18: BAT1.-, BAT2.+

notes:
  PINES RF
  SCK 13
  MISO 12
  MOSI 11
  CE 9
  CSN 10
  IN= 7 V - 12 V

custom parts:
  L298N DC motor driver: 2x DC motor driver with 78M05 positive voltage regulator (7..35 V) L298N: max 46 V, 2 A Set 5 V Enable jumper to enable 5 V regultor (needed for the L298N) and +5 V output at screw terminal or supply external +5 V at screw terminal Set ENA and/or ENB to +5 V to enable motor permanently or supply ENA and/or ENB with PWM signal IN1 and IN2 set rotation directory for motor A (OUT1/OUT2) IN2 and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
  18650 battery holder: 18650 Battery Holder
