# Fritzing sketch Control (saved by Fritzing 0.9.10b)
breadboards: 1

parts:
  S1 = Pushbutton [package="[THT]"]
  S2 = Pushbutton [package="[THT]"]
  S3 = Pushbutton [package="[THT]"]
  S4 = Pushbutton [package="[THT]"]
  S5 = Pushbutton [package="[THT]"]
  Componente1 = NRF24L01+ Breakout Board
  S6 = SPST Switch [package=r_sw_th]
  Componente2 = Arduino Pro Mini v13
  U1 = V_REG_LD1117VXX [package=78xxl]
  C1 = Electrolytic Capacitor [capacitance=1µF package="100 mil [THT, electrolytic]"]
  BAT1 = 18650 battery holder [package=battery-18650-kit]
  BAT2 = 18650 battery holder [package=battery-18650-kit]

nets:
  GND: S1.Pin_1, S1.Pin_2, S2.Pin_1, S2.Pin_2, S3.Pin_1, S3.Pin_2, S4.Pin_1, S4.Pin_2, S5.Pin_1, S5.Pin_2, Componente1.GND, Componente2.GND, U1.GND, C1.-, BAT2.-
  N1: S1.Pin_3, S1.Pin_4, Componente2.D5_PWM
  N2: S2.Pin_3, S2.Pin_4, Componente2.D4
  N3: S3.Pin_3, S3.Pin_4, Componente2.D6_PWM
  N4: S4.Pin_3, S4.Pin_4, Componente2.D7
  N5: S5.Pin_3, S5.Pin_4, Componente2.D8
  N6: Componente1.VCC, U1.OUT
  N7: Componente1.CE, Componente2.D9_PWM
  N8: Componente1.CS, Componente2.D10_PWM/SS
  N9: Componente1.SCK, Componente2.D13/SCK
  N10: Componente1.MOSI, Componente2.D11_PWM/MOSI
  N11: Componente1.MISO, Componente2.D12/MISO
  N12: S6.P, Componente2.RAW, U1.IN, C1.+
  N13: S6.S, BAT1.+
  N14: BAT1.-, BAT2.+

notes:
  PINES RF
  SCK 13
  MISO 12
  MOSI 11
  CE 9
  CSN 10
  IN= 7 V - 12 V

custom parts:
  18650 battery holder: 18650 Battery Holder
